// Logisim project 1607065_1607062_SAP1.circ as structural Verilog: 13 circuits, main circuit main
module main (
  input  CPU_CLR
);

  wire CPU_CLK_out, cs_1_clk, cs_1_clr, cs_1_cp, cs_1_ea, cs_1_ep, cs_1_eu, cs_1_nce, cs_1_nclk, cs_1_nei,
       cs_1_nla, cs_1_nlb, cs_1_nli, cs_1_nlm, cs_1_nlo, cs_1_su, not_1_out;
  wire [3:0] ir_1_to_controller, mar_1_to_ram, or_1_to_binary_display, or_1_to_binary_display_2,
       pc_1_output_to_bus;
  wire [7:0] acm_1_to_add_sub, br_1_to_adder_subtractor;
  wire [7:4] pc_1_output_to_bus_2;

  Clock CPU_CLK (.out(CPU_CLK_out));
  not not_1 (not_1_out, cs_1_nce);
  PC pc_1 (
    .Cp(cs_1_cp), .nClk(cs_1_nclk), .Output_to_Bus({pc_1_output_to_bus_2, pc_1_output_to_bus}), .Ep(cs_1_ep),
    .CLR(cs_1_clr));
  MAR mar_1 (
    .Clk(cs_1_clk), .CLR(cs_1_clr), .From_Bus({pc_1_output_to_bus_2, pc_1_output_to_bus}),
    .To_RAM(mar_1_to_ram), .nLm(cs_1_nlm));
  IR ir_1 (
    .To_Controller(ir_1_to_controller), .Clk(cs_1_clk), .CLR(cs_1_clr),
    .From_Bus({pc_1_output_to_bus_2, pc_1_output_to_bus}),
    .To_Bus({pc_1_output_to_bus_2, pc_1_output_to_bus}), .nLi(cs_1_nli), .nEi(cs_1_nei));
  RAM #(.addrWidth(4)) ram_1 (
    .addr(mar_1_to_ram), .data({pc_1_output_to_bus_2, pc_1_output_to_bus}), .sel(not_1_out), .clk(cs_1_clk),
    .ld(not_1_out), .clr(cs_1_clr));
  CS cs_1 (
    .I7(ir_1_to_controller[3]), .I6(ir_1_to_controller[2]), .I5(ir_1_to_controller[1]),
    .I4(ir_1_to_controller[0]), .Cp(cs_1_cp), .Ep(cs_1_ep), .nLm(cs_1_nlm), .nCE(cs_1_nce), .nLi(cs_1_nli),
    .nEi(cs_1_nei), .nLa(cs_1_nla), .Ea(cs_1_ea), .Su(cs_1_su), .Eu(cs_1_eu), .nLb(cs_1_nlb), .nLo(cs_1_nlo),
    .CPU_CLK(CPU_CLK_out), .CPU_CLR(CPU_CLR), .Clk(cs_1_clk), .nClk(cs_1_nclk), .CLR(cs_1_clr));  // open: nCLR
  ACM acm_1 (
    .To_Add_Sub(acm_1_to_add_sub), .Clk(cs_1_clk), .CLR(cs_1_clr),
    .From_Bus({pc_1_output_to_bus_2, pc_1_output_to_bus}),
    .To_Bus({pc_1_output_to_bus_2, pc_1_output_to_bus}), .nLa(cs_1_nla), .Ea(cs_1_ea));
  AS as_1 (
    .From_B_register(br_1_to_adder_subtractor), .To_Bus({pc_1_output_to_bus_2, pc_1_output_to_bus}),
    .From_Accumulator(acm_1_to_add_sub), .Su(cs_1_su), .Eu(cs_1_eu));
  BR br_1 (
    .Clk(cs_1_clk), .CLR(cs_1_clr), .From_Bus({pc_1_output_to_bus_2, pc_1_output_to_bus}),
    .To_Adder_Subtractor(br_1_to_adder_subtractor), .nLb(cs_1_nlb));
  OR or_1 (
    .Clk(cs_1_clk), .CLR(cs_1_clr), .From_Bus({pc_1_output_to_bus_2, pc_1_output_to_bus}),
    .To_Binary_Display({or_1_to_binary_display_2, or_1_to_binary_display}), .nLo(cs_1_nlo));
  Hex_Digit_Display hex_digit_display_1 (.value(pc_1_output_to_bus_2));  // open: dp
  Hex_Digit_Display hex_digit_display_2 (.value(or_1_to_binary_display_2));  // open: dp
  Hex_Digit_Display hex_digit_display_3 (.value(pc_1_output_to_bus));  // open: dp
  Hex_Digit_Display hex_digit_display_4 (.value(or_1_to_binary_display));  // open: dp

  // Notes on the sheet:
  //   1607065_1607062_SAP_1_MAIN CIRCUIT
  //   Data in the bus
  //   Data Output
endmodule

// P/C
module PC (
  input  Cp,
  input  nClk,
  input  Ep,
  input  CLR,
  output [7:0] Output_to_Bus
);

  wire ha_1_sun, ha_2_carry, ha_2_sun, ha_3_carry, ha_3_sun, ha_4_carry, ha_4_sun, ha_5_carry, ha_5_sun,
       ha_6_carry, ha_6_sun, ha_7_carry, ha_7_sun, ha_8_carry, ha_8_sun, not_1_out;
  wire [7:0] d_ff_8_q;

  not not_1 (not_1_out, nClk);
  HA ha_1 (.A(d_ff_8_q[7]), .B(ha_2_carry), .Sun(ha_1_sun));  // open: Carry
  D_Flip_Flop d_ff_1 (.clk(not_1_out), .D(ha_1_sun), .Q(d_ff_8_q[7]), .reset(CLR));  // open: Qn, preset, en
  HA ha_2 (.A(d_ff_8_q[6]), .B(ha_3_carry), .Sun(ha_2_sun), .Carry(ha_2_carry));
  D_Flip_Flop d_ff_2 (.clk(not_1_out), .D(ha_2_sun), .Q(d_ff_8_q[6]), .reset(CLR));  // open: Qn, preset, en
  HA ha_3 (.A(d_ff_8_q[5]), .B(ha_4_carry), .Sun(ha_3_sun), .Carry(ha_3_carry));
  D_Flip_Flop d_ff_3 (.clk(not_1_out), .D(ha_3_sun), .Q(d_ff_8_q[5]), .reset(CLR));  // open: Qn, preset, en
  HA ha_4 (.A(d_ff_8_q[4]), .B(ha_5_carry), .Sun(ha_4_sun), .Carry(ha_4_carry));
  D_Flip_Flop d_ff_4 (.clk(not_1_out), .D(ha_4_sun), .Q(d_ff_8_q[4]), .reset(CLR));  // open: Qn, preset, en
  HA ha_5 (.A(d_ff_8_q[3]), .B(ha_6_carry), .Sun(ha_5_sun), .Carry(ha_5_carry));
  D_Flip_Flop d_ff_5 (.clk(not_1_out), .D(ha_5_sun), .Q(d_ff_8_q[3]), .reset(CLR));  // open: Qn, preset, en
  HA ha_6 (.A(d_ff_8_q[2]), .B(ha_7_carry), .Sun(ha_6_sun), .Carry(ha_6_carry));
  D_Flip_Flop d_ff_6 (.clk(not_1_out), .D(ha_6_sun), .Q(d_ff_8_q[2]), .reset(CLR));  // open: Qn, preset, en
  HA ha_7 (.A(d_ff_8_q[1]), .B(ha_8_carry), .Sun(ha_7_sun), .Carry(ha_7_carry));
  D_Flip_Flop d_ff_7 (.clk(not_1_out), .D(ha_7_sun), .Q(d_ff_8_q[1]), .reset(CLR));  // open: Qn, preset, en
  HA ha_8 (.A(d_ff_8_q[0]), .B(Cp), .Sun(ha_8_sun), .Carry(ha_8_carry));
  D_Flip_Flop d_ff_8 (.clk(not_1_out), .D(ha_8_sun), .Q(d_ff_8_q[0]), .reset(CLR));  // open: Qn, preset, en
  assign Output_to_Bus = Ep ? d_ff_8_q : 8'bz;  // Controlled_Buffer controlled_buffer_1

  // Notes on the sheet:
  //   1607065_SAP_1_Program_Counter
endmodule

module HA (
  input  A,
  input  B,
  output Sun,
  output Carry
);

  xor xor_1 (Sun, A, B);
  and and_1 (Carry, A, B);

  // Notes on the sheet:
  //   1607065_SAP_1_HALF_ADDER
endmodule

module MAR (
  input  Clk,
  input  CLR,
  input  [7:0] From_Bus,
  input  nLm,
  output [3:0] To_RAM
);

  wire not_1_out;
  wire [7:0] controlled_buffer_1_out;

  assign {{4{controlled_buffer_1_out[7]}}, controlled_buffer_1_out[3:0]} = not_1_out ? From_Bus : 8'bz;  // Controlled_Buffer controlled_buffer_1
  not not_1 (not_1_out, nLm);
  D_Flip_Flop d_ff_1 (.clk(Clk), .D(controlled_buffer_1_out[3]), .Q(To_RAM[3]), .reset(CLR));  // open: Qn, preset, en
  D_Flip_Flop d_ff_2 (.clk(Clk), .D(controlled_buffer_1_out[2]), .Q(To_RAM[2]), .reset(CLR));  // open: Qn, preset, en
  D_Flip_Flop d_ff_3 (.clk(Clk), .D(controlled_buffer_1_out[1]), .Q(To_RAM[1]), .reset(CLR));  // open: Qn, preset, en
  D_Flip_Flop d_ff_4 (.clk(Clk), .D(controlled_buffer_1_out[0]), .Q(To_RAM[0]), .reset(CLR));  // open: Qn, preset, en
  // also tied to GND on the sheet: controlled_buffer_1_out[7]

  // Notes on the sheet:
  //   1607065_SAP_1_MAR
endmodule

// I/R
module IR (
  input  nEi,
  input  Clk,
  input  CLR,
  input  [7:0] From_Bus,
  input  nLi,
  output [3:0] To_Controller,
  output [7:0] To_Bus
);

  wire not_1_out, not_2_out;
  wire [3:0] D0_q;
  wire [7:0] controlled_buffer_1_out;

  D_Flip_Flop D7 (
    .clk(Clk), .D(controlled_buffer_1_out[7]), .Q(To_Controller[3]), .reset(CLR));  // open: Qn, preset, en
  assign controlled_buffer_1_out = not_1_out ? From_Bus : 8'bz;  // Controlled_Buffer controlled_buffer_1
  not not_1 (not_1_out, nLi);
  D_Flip_Flop D6 (
    .clk(Clk), .D(controlled_buffer_1_out[6]), .Q(To_Controller[2]), .reset(CLR));  // open: Qn, preset, en
  D_Flip_Flop D5 (
    .clk(Clk), .D(controlled_buffer_1_out[5]), .Q(To_Controller[1]), .reset(CLR));  // open: Qn, preset, en
  D_Flip_Flop D4 (
    .clk(Clk), .D(controlled_buffer_1_out[4]), .Q(To_Controller[0]), .reset(CLR));  // open: Qn, preset, en
  not not_2 (not_2_out, nEi);
  D_Flip_Flop D3 (.clk(Clk), .D(controlled_buffer_1_out[3]), .Q(D0_q[3]), .reset(CLR));  // open: Qn, preset, en
  assign To_Bus = not_2_out ? {4'b0000, D0_q} : 8'bz;  // Controlled_Buffer controlled_buffer_2
  D_Flip_Flop D2 (.clk(Clk), .D(controlled_buffer_1_out[2]), .Q(D0_q[2]), .reset(CLR));  // open: Qn, preset, en
  D_Flip_Flop D1 (.clk(Clk), .D(controlled_buffer_1_out[1]), .Q(D0_q[1]), .reset(CLR));  // open: Qn, preset, en
  D_Flip_Flop D0 (.clk(Clk), .D(controlled_buffer_1_out[0]), .Q(D0_q[0]), .reset(CLR));  // open: Qn, preset, en

  // Notes on the sheet:
  //   1607065_SAP_1_INSTRUCTION_REGISTER
endmodule

// C/S
module CS (
  input  CPU_CLK,
  input  CPU_CLR,
  input  I7,
  input  I6,
  input  I5,
  input  I4,
  output Clk,
  output nClk,
  output nCLR,
  output CLR,
  output Cp,
  output Ep,
  output nLm,
  output nCE,
  output nLi,
  output nEi,
  output nLa,
  output Ea,
  output Su,
  output Eu,
  output nLb,
  output nLo
);

  wire and_1_out, and_2_out, and_3_out, and_4_out, and_5_out, and_6_out, and_7_out, and_8_out, and_9_out,
       and_10_out, and_11_out, and_12_out, and_15_out, and_16_out, and_17_out, and_18_out, id_1_add,
       id_1_hlt, id_1_lda, id_1_out, id_1_sub, rc_1_t3, rc_1_t4, rc_1_t5, rc_1_t6;

  ID id_1 (
    .I7(I7), .I6(I6), .I5(I5), .I4(I4), .LDA(id_1_lda), .ADD(id_1_add), .SUB(id_1_sub), .OUT(id_1_out),
    .HLT(id_1_hlt));
  RC rc_1 (
    .HLT(id_1_hlt), .CPU_Clk(CPU_CLK), .CPU_CLR(CPU_CLR), .T1(Ep), .T2(Cp), .T3(rc_1_t3), .T4(rc_1_t4),
    .T5(rc_1_t5), .T6(rc_1_t6), .Clk(Clk), .nClk(nClk), .nCLR(nCLR), .CLR(CLR));
  and and_1 (and_1_out, id_1_lda, rc_1_t4);
  and and_2 (and_2_out, id_1_add, rc_1_t4);
  nor nor_1 (nLm, Ep, and_1_out, and_2_out, and_3_out);
  Hex_Digit_Display hex_digit_display_1 (.value({Cp, Ep, nLm, nCE}));  // open: dp
  and and_3 (and_3_out, id_1_sub, rc_1_t4);
  and and_4 (and_4_out, id_1_lda, rc_1_t5);
  and and_5 (and_5_out, id_1_add, rc_1_t5);
  nor nor_2 (nCE, rc_1_t3, and_4_out, and_5_out, and_6_out);
  and and_6 (and_6_out, id_1_sub, rc_1_t5);
  not not_1 (nLi, rc_1_t3);
  and and_7 (and_7_out, id_1_lda, rc_1_t4);
  and and_8 (and_8_out, id_1_add, rc_1_t4);
  nor nor_3 (nEi, and_7_out, and_8_out, and_9_out);
  and and_9 (and_9_out, id_1_sub, rc_1_t4);
  and and_10 (and_10_out, id_1_lda, rc_1_t5);
  Hex_Digit_Display hex_digit_display_2 (.value({nLi, nEi, nLa, Ea}));  // open: dp
  and and_11 (and_11_out, id_1_add, rc_1_t6);
  nor nor_4 (nLa, and_10_out, and_11_out, and_12_out);
  and and_12 (and_12_out, id_1_sub, rc_1_t6);
  and and_13 (Ea, id_1_out, rc_1_t4);
  and and_14 (Su, id_1_sub, rc_1_t6);
  and and_15 (and_15_out, id_1_add, rc_1_t6);
  or or_1 (Eu, and_15_out, and_16_out);
  and and_16 (and_16_out, id_1_sub, rc_1_t6);
  Hex_Digit_Display hex_digit_display_3 (.value({Su, Eu, nLb, nLo}));  // open: dp
  and and_17 (and_17_out, id_1_sub, rc_1_t5);
  and and_18 (and_18_out, id_1_add, rc_1_t5);
  nor nor_5 (nLb, and_18_out, and_17_out);
  nand nand_1 (nLo, rc_1_t4, id_1_out);

  // Notes on the sheet:
  //   1607065_SAP_1_CONTROLLER_SEQUENCE
endmodule

// R/C
module RC (
  input  HLT,
  input  CPU_Clk,
  input  CPU_CLR,
  output Clk,
  output nClk,
  output nCLR,
  output CLR,
  output T1,
  output T2,
  output T3,
  output T4,
  output T5,
  output T6
);

  wire j_k_ff_1_q, j_k_ff_2_qn, j_k_ff_3_qn, j_k_ff_4_qn, j_k_ff_5_qn, j_k_ff_6_qn, not_1_out;

  not not_1 (not_1_out, HLT);
  and and_1 (Clk, not_1_out, CPU_Clk);
  J_K_Flip_Flop j_k_ff_1 (
    .J(j_k_ff_6_qn), .clk(Clk), .K(T6), .Q(j_k_ff_1_q), .Qn(T1), .reset(CPU_CLR));  // open: preset, en
  J_K_Flip_Flop j_k_ff_2 (
    .J(T1), .clk(Clk), .K(j_k_ff_1_q), .Q(T2), .Qn(j_k_ff_2_qn), .reset(CPU_CLR));  // open: preset, en
  J_K_Flip_Flop j_k_ff_3 (
    .J(T2), .clk(Clk), .K(j_k_ff_2_qn), .Q(T3), .Qn(j_k_ff_3_qn), .reset(CPU_CLR));  // open: preset, en
  J_K_Flip_Flop j_k_ff_4 (
    .J(T3), .clk(Clk), .K(j_k_ff_3_qn), .Q(T4), .Qn(j_k_ff_4_qn), .reset(CPU_CLR));  // open: preset, en
  J_K_Flip_Flop j_k_ff_5 (
    .J(T4), .clk(Clk), .K(j_k_ff_4_qn), .Q(T5), .Qn(j_k_ff_5_qn), .reset(CPU_CLR));  // open: preset, en
  J_K_Flip_Flop j_k_ff_6 (
    .J(T5), .clk(Clk), .K(j_k_ff_5_qn), .Q(T6), .Qn(j_k_ff_6_qn), .reset(CPU_CLR));  // open: preset, en
  not not_2 (nClk, Clk);
  not not_3 (nCLR, CPU_CLR);

  assign CLR = CPU_CLR;

  // Notes on the sheet:
  //   1607065_SAP_1_RING_COUNTER
endmodule

// I/D
module ID (
  input  I7,
  input  I6,
  input  I5,
  input  I4,
  output LDA,
  output ADD,
  output SUB,
  output OUT,
  output HLT
);

  wire not_1_out, not_2_out, not_3_out, not_4_out;

  not not_1 (not_1_out, I7);
  not not_2 (not_2_out, I6);
  not not_3 (not_3_out, I5);
  not not_4 (not_4_out, I4);
  and and_1 (LDA, not_1_out, not_2_out, not_3_out, not_4_out);
  and and_2 (ADD, not_1_out, not_2_out, not_3_out, I4);
  and and_3 (SUB, not_1_out, not_2_out, I5, not_4_out);
  and and_4 (OUT, I7, I6, I5, not_4_out);
  and and_5 (HLT, I7, I6, I5, I4);

  // Notes on the sheet:
  //   1607065_SAP_1_INSTRUCTION_DECODER
endmodule

// AC
module ACM (
  input  Ea,
  input  Clk,
  input  CLR,
  input  [7:0] From_Bus,
  input  nLa,
  output [7:0] To_Bus,
  output [7:0] To_Add_Sub
);

  wire not_1_out;
  wire [7:0] controlled_buffer_1_out;

  D_Flip_Flop D7 (.clk(Clk), .D(controlled_buffer_1_out[7]), .Q(To_Add_Sub[7]), .reset(CLR));  // open: Qn, preset, en
  not not_1 (not_1_out, nLa);
  assign controlled_buffer_1_out = not_1_out ? From_Bus : 8'bz;  // Controlled_Buffer controlled_buffer_1
  D_Flip_Flop d_ff_1 (
    .clk(Clk), .D(controlled_buffer_1_out[6]), .Q(To_Add_Sub[6]), .reset(CLR));  // open: Qn, preset, en
  D_Flip_Flop d_ff_2 (
    .clk(Clk), .D(controlled_buffer_1_out[5]), .Q(To_Add_Sub[5]), .reset(CLR));  // open: Qn, preset, en
  D_Flip_Flop d_ff_3 (
    .clk(Clk), .D(controlled_buffer_1_out[4]), .Q(To_Add_Sub[4]), .reset(CLR));  // open: Qn, preset, en
  assign To_Bus = Ea ? To_Add_Sub : 8'bz;  // Controlled_Buffer controlled_buffer_2
  D_Flip_Flop d_ff_4 (
    .clk(Clk), .D(controlled_buffer_1_out[3]), .Q(To_Add_Sub[3]), .reset(CLR));  // open: Qn, preset, en
  D_Flip_Flop d_ff_5 (
    .clk(Clk), .D(controlled_buffer_1_out[2]), .Q(To_Add_Sub[2]), .reset(CLR));  // open: Qn, preset, en
  D_Flip_Flop d_ff_6 (
    .clk(Clk), .D(controlled_buffer_1_out[1]), .Q(To_Add_Sub[1]), .reset(CLR));  // open: Qn, preset, en
  D_Flip_Flop D0 (.clk(Clk), .D(controlled_buffer_1_out[0]), .Q(To_Add_Sub[0]), .reset(CLR));  // open: Qn, preset, en

  // Notes on the sheet:
  //   1607062_SAP_1_ACCUMULATOR
endmodule

// ADDSUB
module AS (
  input  [7:0] From_B_register,
  input  Su,
  input  Eu,
  input  [7:0] From_Accumulator,
  output [7:0] To_Bus
);

  wire fa_2_c_2, fa_3_c_2, fa_4_c_2, fa_5_c_2, fa_6_c_2, fa_7_c_2, fa_8_c_2, xor_1_out, xor_2_out, xor_3_out,
       xor_4_out, xor_5_out, xor_6_out, xor_7_out, xor_8_out;
  wire [7:0] fa_8_s;

  assign To_Bus = Eu ? fa_8_s : 8'bz;  // Controlled_Buffer controlled_buffer_1
  FA fa_1 (.C(fa_2_c_2), .X(From_Accumulator[7]), .Y(xor_1_out), .S(fa_8_s[7]));  // open: C_2
  xor xor_1 (xor_1_out, Su, From_B_register[7]);
  FA fa_2 (.C(fa_3_c_2), .X(From_Accumulator[6]), .Y(xor_2_out), .S(fa_8_s[6]), .C_2(fa_2_c_2));
  xor xor_2 (xor_2_out, Su, From_B_register[6]);
  FA fa_3 (.C(fa_4_c_2), .X(From_Accumulator[5]), .Y(xor_3_out), .S(fa_8_s[5]), .C_2(fa_3_c_2));
  xor xor_3 (xor_3_out, Su, From_B_register[5]);
  FA fa_4 (.C(fa_5_c_2), .X(From_Accumulator[4]), .Y(xor_4_out), .S(fa_8_s[4]), .C_2(fa_4_c_2));
  xor xor_4 (xor_4_out, Su, From_B_register[4]);
  xor xor_5 (xor_5_out, Su, From_B_register[3]);
  FA fa_5 (.C(fa_6_c_2), .X(From_Accumulator[3]), .Y(xor_5_out), .S(fa_8_s[3]), .C_2(fa_5_c_2));
  xor xor_6 (xor_6_out, Su, From_B_register[2]);
  FA fa_6 (.C(fa_7_c_2), .X(From_Accumulator[2]), .Y(xor_6_out), .S(fa_8_s[2]), .C_2(fa_6_c_2));
  FA fa_7 (.C(fa_8_c_2), .X(From_Accumulator[1]), .Y(xor_7_out), .S(fa_8_s[1]), .C_2(fa_7_c_2));
  xor xor_7 (xor_7_out, Su, From_B_register[1]);
  FA fa_8 (.C(Su), .X(From_Accumulator[0]), .Y(xor_8_out), .S(fa_8_s[0]), .C_2(fa_8_c_2));
  xor xor_8 (xor_8_out, Su, From_B_register[0]);

  // Notes on the sheet:
  //   1607062_SAP_1_ADDER SUBTRACTOR
endmodule

// F/A
module FA (
  input  C,
  input  X,
  input  Y,
  output S,
  output C_2
);

  wire and_1_out, and_2_out, xor_1_out;

  xor xor_1 (xor_1_out, X, Y);
  and and_1 (and_1_out, X, Y);
  xor xor_2 (S, xor_1_out, C);
  and and_2 (and_2_out, xor_1_out, C);
  or or_1 (C_2, and_2_out, and_1_out);

  // Notes on the sheet:
  //   1607062_SAP_1_FULL ADDER
endmodule

// B
module BR (
  input  Clk,
  input  CLR,
  input  [7:0] From_Bus,
  input  nLb,
  output [7:0] To_Adder_Subtractor
);

  wire not_1_out;
  wire [7:0] controlled_buffer_1_out;

  assign controlled_buffer_1_out = not_1_out ? From_Bus : 8'bz;  // Controlled_Buffer controlled_buffer_1
  not not_1 (not_1_out, nLb);
  D_Flip_Flop D7 (
    .clk(Clk), .D(controlled_buffer_1_out[7]), .Q(To_Adder_Subtractor[7]), .reset(CLR));  // open: Qn, preset, en
  D_Flip_Flop d_ff_1 (
    .clk(Clk), .D(controlled_buffer_1_out[6]), .Q(To_Adder_Subtractor[6]), .reset(CLR));  // open: Qn, preset, en
  D_Flip_Flop d_ff_2 (
    .clk(Clk), .D(controlled_buffer_1_out[5]), .Q(To_Adder_Subtractor[5]), .reset(CLR));  // open: Qn, preset, en
  D_Flip_Flop d_ff_3 (
    .clk(Clk), .D(controlled_buffer_1_out[4]), .Q(To_Adder_Subtractor[4]), .reset(CLR));  // open: Qn, preset, en
  D_Flip_Flop d_ff_4 (
    .clk(Clk), .D(controlled_buffer_1_out[3]), .Q(To_Adder_Subtractor[3]), .reset(CLR));  // open: Qn, preset, en
  D_Flip_Flop d_ff_5 (
    .clk(Clk), .D(controlled_buffer_1_out[2]), .Q(To_Adder_Subtractor[2]), .reset(CLR));  // open: Qn, preset, en
  D_Flip_Flop d_ff_6 (
    .clk(Clk), .D(controlled_buffer_1_out[1]), .Q(To_Adder_Subtractor[1]), .reset(CLR));  // open: Qn, preset, en
  D_Flip_Flop D0 (
    .clk(Clk), .D(controlled_buffer_1_out[0]), .Q(To_Adder_Subtractor[0]), .reset(CLR));  // open: Qn, preset, en

  // Notes on the sheet:
  //   1607062_SAP_1_B_REGISTER
endmodule

// O/R
module OR (
  input  Clk,
  input  CLR,
  input  [7:0] From_Bus,
  input  nLo,
  output [7:0] To_Binary_Display
);

  wire not_1_out;
  wire [7:0] controlled_buffer_1_out;

  assign controlled_buffer_1_out = not_1_out ? From_Bus : 8'bz;  // Controlled_Buffer controlled_buffer_1
  not not_1 (not_1_out, nLo);
  D_Flip_Flop D7 (
    .clk(Clk), .D(controlled_buffer_1_out[7]), .Q(To_Binary_Display[7]), .reset(CLR));  // open: Qn, preset, en
  D_Flip_Flop d_ff_1 (
    .clk(Clk), .D(controlled_buffer_1_out[6]), .Q(To_Binary_Display[6]), .reset(CLR));  // open: Qn, preset, en
  D_Flip_Flop d_ff_2 (
    .clk(Clk), .D(controlled_buffer_1_out[5]), .Q(To_Binary_Display[5]), .reset(CLR));  // open: Qn, preset, en
  D_Flip_Flop d_ff_3 (
    .clk(Clk), .D(controlled_buffer_1_out[4]), .Q(To_Binary_Display[4]), .reset(CLR));  // open: Qn, preset, en
  D_Flip_Flop d_ff_4 (
    .clk(Clk), .D(controlled_buffer_1_out[3]), .Q(To_Binary_Display[3]), .reset(CLR));  // open: Qn, preset, en
  D_Flip_Flop d_ff_5 (
    .clk(Clk), .D(controlled_buffer_1_out[2]), .Q(To_Binary_Display[2]), .reset(CLR));  // open: Qn, preset, en
  D_Flip_Flop d_ff_6 (
    .clk(Clk), .D(controlled_buffer_1_out[1]), .Q(To_Binary_Display[1]), .reset(CLR));  // open: Qn, preset, en
  D_Flip_Flop D0 (
    .clk(Clk), .D(controlled_buffer_1_out[0]), .Q(To_Binary_Display[0]), .reset(CLR));  // open: Qn, preset, en

  // Notes on the sheet:
  //   1607062_SAP_1_OUTPUT_REGISTER
endmodule
